// Logisim project capex.circ as structural Verilog: 1 circuit, main circuit main
module main (
  output imm2,
  output imm1,
  output [7:0] nextpc,
  output [7:0] instruction,
  output Write,
  output [2:0] WriteReg,
  output [7:0] Memoryaddress,
  output [7:0] MemOut,
  output [7:0] RegData1,
  output [7:0] RegData2,
  output operation,
  output [7:0] Memwrite,
  output [7:0] ALUO,
  output [7:0] RegDataW,
  output [2:0] ReadReg1,
  output [2:0] ReadReg2,
  output MemR,
  output MemW
);

  wire and_1_out, and_2_out, and_3_out, and_4_out, and_5_out, and_6_out, and_7_out, and_8_out,
       clockcycle_out, decoder_1_out0, decoder_1_out1, decoder_1_out2, decoder_1_out3, decoder_1_out4,
       decoder_1_out5, decoder_1_out6, decoder_1_out7;
  wire [7:0] adder_2_out, multiplexer_4_out, PC_q, r0_q, r1_q, r2_q, r3_q, r4_q, r5_q, r6_q, r7_q,
       subtractor_1_out;
  wire [23:0] ram_1_dout;

  Register PC (.D(instruction), .en(1'b1), .clk(clockcycle_out), .Q(PC_q));  // open: clr
  Clock clockcycle (.out(clockcycle_out));
  Adder adder_1 (.a(8'h1), .b(PC_q), .out(instruction));  // open: cin, cout
  RAM #(.dataWidth(32), .enables("line")) ram_1 (
    .addr(PC_q), .we(1'b0), .clk(clockcycle_out),
    .dout({Write, WriteReg, imm1, ReadReg1, ram_1_dout[23:19], imm2, ReadReg1, ram_1_dout[14:10], operation, ram_1_dout[8:3], MemR, MemW, ram_1_dout[0]}));  // open: din
  Decoder #(.select(3)) decoder_1 (
    .out0(decoder_1_out0), .out1(decoder_1_out1), .out2(decoder_1_out2), .out3(decoder_1_out3),
    .out4(decoder_1_out4), .out5(decoder_1_out5), .out6(decoder_1_out6), .out7(decoder_1_out7), .sel(WriteReg));  // open: en
  Register r0 (.D(RegDataW), .en(and_1_out), .clk(clockcycle_out), .Q(r0_q));  // open: clr
  and and_1 (and_1_out, decoder_1_out0, Write);
  Register r1 (.D(RegDataW), .en(and_2_out), .clk(clockcycle_out), .Q(r1_q));  // open: clr
  and and_2 (and_2_out, decoder_1_out1, Write);
  Register r2 (.D(RegDataW), .en(and_3_out), .clk(clockcycle_out), .Q(r2_q));  // open: clr
  and and_3 (and_3_out, decoder_1_out2, Write);
  Register r3 (.D(RegDataW), .en(and_4_out), .clk(clockcycle_out), .Q(r3_q));  // open: clr
  and and_4 (and_4_out, decoder_1_out3, Write);
  Register r4 (.D(RegDataW), .en(and_5_out), .clk(clockcycle_out), .Q(r4_q));  // open: clr
  and and_5 (and_5_out, decoder_1_out4, Write);
  Register r5 (.D(RegDataW), .en(and_6_out), .clk(clockcycle_out), .Q(r5_q));  // open: clr
  and and_6 (and_6_out, decoder_1_out5, Write);
  Register r6 (.D(RegDataW), .en(and_7_out), .clk(clockcycle_out), .Q(r6_q));  // open: clr
  and and_7 (and_7_out, decoder_1_out6, Write);
  Register r7 (.D(RegDataW), .en(and_8_out), .clk(clockcycle_out), .Q(r7_q));  // open: clr
  and and_8 (and_8_out, decoder_1_out7, Write);
  Multiplexer #(.select(3), .width(8)) multiplexer_1 (
    .in0(r0_q), .in1(r1_q), .in2(r2_q), .in3(r3_q), .in4(r4_q), .in5(r5_q), .in6(r6_q), .in7(r7_q),
    .out(RegData1), .sel(ReadReg1));
  Multiplexer #(.select(3), .width(8)) multiplexer_2 (
    .in0(r0_q), .in1(r1_q), .in2(r2_q), .in3(r3_q), .in4(r4_q), .in5(r5_q), .in6(r6_q), .in7(r7_q),
    .out(Memwrite), .sel(ReadReg1));
  Multiplexer #(.width(8)) multiplexer_3 (
    .in0(RegData1), .in1({ReadReg1, ram_1_dout[23:19]}), .out(Memoryaddress), .sel(imm1));
  Multiplexer #(.width(8)) multiplexer_4 (
    .in0(Memwrite), .in1({ReadReg1, ram_1_dout[14:10]}), .out(multiplexer_4_out), .sel(imm2));
  Adder adder_2 (.a(Memoryaddress), .b(multiplexer_4_out), .out(adder_2_out));  // open: cin, cout
  Subtractor subtractor_1 (.a(Memoryaddress), .b(multiplexer_4_out), .out(subtractor_1_out));  // open: bin, bout
  Multiplexer #(.width(8)) multiplexer_5 (.in0(ALUO), .in1(MemOut), .out(RegDataW), .sel(MemR));
  RAM #(.enables("line")) ram_2 (.addr(Memoryaddress), .we(MemW), .clk(clockcycle_out), .din(Memwrite), .dout(MemOut));
  Multiplexer #(.width(8)) multiplexer_6 (.in0(adder_2_out), .in1(subtractor_1_out), .out(ALUO), .sel(operation));

  assign nextpc = instruction;
  assign ReadReg2 = ReadReg1;
  assign RegData2 = Memwrite;

  // Notes on the sheet:
  //   Bekkerman
  //   Tristan Mikiewicz and Josh
  //   Apex(Legends) Processing 
  //   Unit
  //   I have abided by the Stevens
  //   Honor System
  //   I pledge my honor that 
  //   Instruction Memory
endmodule
